# Fritzing sketch romi (saved by Fritzing 0.9.6b)
circuit board: 9.05228cm x 5.7785cm
breadboards: 1

parts:
  PIC_left = PIC16F1705 [part_number=PIC16F1705 package="DIP (Dual Inline) [THT]"]
  PIC_right = PIC16F1705 [part_number=PIC16F1705 package="DIP (Dual Inline) [THT]"]
  SDA = Resistor [tolerance=±5% resistance=10000 power=0.25 package=THT]
  MCLR = Resistor [tolerance=±5% resistance=10000 power=0.25 package=THT]
  led_left = Resistor [tolerance=±5% resistance=1k power=0.25 package=THT]
  led_right = Resistor [tolerance=±5% resistance=1k power=0.25 package=THT]
  LED_left = LED - 3mm [color="Red (633nm)" current=0.030 package="3 mm [THT]"]
  LED_right = LED - 3mm [color="Red (633nm)" current=0.030 package="3 mm [THT]"]
  PWR_5v = Screw terminal - 2 pins [package=THT]
  SCL = Resistor [tolerance=±5% resistance=10000 power=0.25 package=THT]
  RST = SWITCH-MOMENTARY-2 [package=tactile-pth]
  MOTOR_right = MOTOR_HEADER
  RST/I2C = Camdenboss CTB0158-3 [part_number=CTB0158-3 package=THT]
  PICKIT_right = PICKIT_3_PROG
  PICKIT_left = PICKIT_3_PROG
  MOTOR_left = PICKIT_3_PROG  # not connected

nets:
  VDD: PIC_left.Vdd, PIC_right.Vdd, PIC_right.RC4, SDA.Pin_0, PWR_5v.pin1, SCL.Pin_0, PICKIT_right.VDD, PICKIT_left.VDD
  N1: PIC_left.MCLR/RA3, PIC_right.MCLR/RA3, MCLR.Pin_1, RST.2, PICKIT_right.Vpp/MCLR, PICKIT_left.Vpp/MCLR
  VSS: PIC_left.RC4, PIC_left.RC2, PIC_right.RC2, led_left.Pin_0, led_right.Pin_0, PWR_5v.pin2, RST.1, PICKIT_right.VSS, PICKIT_left.VSS
  N2: PIC_left.RC3, LED_left.anode
  VSS_2: PIC_left.Vss, PIC_right.Vss, SCL.Pin_1, RST/I2C.pin2
  N3: PIC_left.RA0, PIC_right.RA0, SDA.Pin_1, RST/I2C.pin3
  N4: PIC_left.RC0, PICKIT_left.PGC
  N5: PIC_left.RC1, PICKIT_left.PGD
  N6: PIC_right.RA5, MOTOR_right.DIR
  N7: PIC_right.RA4, MOTOR_right.PWM
  N8: PIC_right.RC5, MOTOR_right.SLP
  N9: PIC_right.RC3, LED_right.anode
  N10: PIC_right.RA1, MOTOR_right.B
  N11: PIC_right.RA2, MOTOR_right.A
  N12: PIC_right.RC0, PICKIT_right.PGC
  N13: PIC_right.RC1, PICKIT_right.PGD
  N14: MCLR.Pin_0, RST/I2C.pin1
  N15: led_left.Pin_1, LED_left.cathode
  N16: led_right.Pin_1, LED_right.cathode

custom parts:
  PIC16F1705: Microchip PIC16F1705
  MOTOR_HEADER: Header for motor driver
  PICKIT_3_PROG: PICKIT 3 6-pin inline header
